// Logisim project Vezje.circ as structural Verilog: 1 circuit, main circuit main
module main (
);

  wire CharA, Clock, comparator_1_eq, counter_3_carry, demultiplexer_2_out0, demultiplexer_2_out1,
       demultiplexer_2_out2, demultiplexer_2_out3, not_1_out, Output, Reset;
  wire [1:0] Counter;
  wire [2:0] Numbers;
  wire [3:0] Input_x0, Input_x1, Input_x2, Input_x3, ROM, X;
  wire [6:0] demultiplexer_1_out0, demultiplexer_1_out1, demultiplexer_1_out2, demultiplexer_1_out3,
       keyboard_1_data;
  wire [6:4] register_1_q, register_2_q, register_3_q, register_4_q, rom_1_data;

  Hex_Digit_Display hex_digit_display_1 (.value(Input_x0));  // open: dp
  not not_1 (not_1_out, Output);
  Hex_Digit_Display hex_digit_display_2 (.value(Input_x1));  // open: dp
  Clock clock_1 (.out(Clock));
  Keyboard #(.buflen(5)) keyboard_1 (.clk(Clock), .re(not_1_out), .clr(Reset), .avail(CharA), .data(keyboard_1_data));
  Hex_Digit_Display hex_digit_display_3 (.value(Input_x3));  // open: dp
  Hex_Digit_Display hex_digit_display_4 (.value(Input_x2));  // open: dp
  Button button_1 (.out(Reset));
  Counter #(.width(3), .max('h4)) counter_1 (.Q(Numbers), .clk(CharA), .clr(Reset));  // open: load, D, count, carry
  LED led_1 (.in(Output));
  Demultiplexer #(.select(2), .width(7)) demultiplexer_1 (
    .out0(demultiplexer_1_out0), .out1(demultiplexer_1_out1), .out2(demultiplexer_1_out2),
    .out3(demultiplexer_1_out3), .in(keyboard_1_data), .sel(Counter), .en(1'b1));
  Counter #(.width(2), .max('h3)) counter_2 (
    .count(Clock), .Q(Counter), .clk(Clock), .clr(Reset));  // open: load, D, carry
  Demultiplexer #(.select(2)) demultiplexer_2 (
    .out0(demultiplexer_2_out0), .out1(demultiplexer_2_out1), .out2(demultiplexer_2_out2),
    .out3(demultiplexer_2_out3), .in(1'b1), .sel(Counter), .en(CharA));
  Register #(.width(7)) register_1 (
    .D(demultiplexer_1_out0), .Q({register_1_q, Input_x3}), .clk(demultiplexer_2_out0), .clr(Reset));  // open: en
  Register #(.width(7)) register_2 (
    .D(demultiplexer_1_out1), .Q({register_2_q, Input_x0}), .clk(demultiplexer_2_out1), .clr(Reset));  // open: en
  Register #(.width(7)) register_3 (
    .D(demultiplexer_1_out2), .Q({register_3_q, Input_x1}), .clk(demultiplexer_2_out2), .clr(Reset));  // open: en
  Register #(.width(7)) register_4 (
    .D(demultiplexer_1_out3), .Q({register_4_q, Input_x2}), .clk(demultiplexer_2_out3), .clr(Reset));  // open: en
  ROM #(.addrWidth(2), .dataWidth(7)) rom_1 (.addr(Counter), .data({rom_1_data, ROM}));  // open: sel
  Comparator #(.width(4)) comparator_1 (.a(X), .b(ROM), .eq(comparator_1_eq));  // open: gt, lt
  Multiplexer #(.select(2), .width(4)) multiplexer_1 (
    .in0(Input_x0), .in1(Input_x1), .in2(Input_x2), .in3(Input_x3), .out(X), .sel(Counter));  // open: en
  Counter #(.width(2), .max('h3)) counter_3 (
    .carry(counter_3_carry), .clk(comparator_1_eq), .clr(Reset));  // open: load, D, count, Q
  Register #(.width(1)) register_5 (
    .D(counter_3_carry), .en(counter_3_carry), .Q(Output), .clk(counter_3_carry), .clr(Reset));

  // Notes on the sheet:
  //   Vhod
  //   contents of rom_1 (hex, n*v repeats v):
  //   1 2 3 4
endmodule
