// Logisim project MIPS.circ as structural Verilog: 7 circuits, main circuit main
module main (
  output [31:0] out_1,
  output [31:0] out_2,
  output [31:0] out_3,
  output [5:0] opcode,
  output [4:0] rs,
  output [4:0] rt,
  output [4:0] rd,
  output [4:0] shamt,
  output [5:0] funct,
  output N,
  output out_11,
  output [1:0] out_12,
  output out_13,
  output out_14,
  output out_15,
  output [1:0] out_16,
  output out_17,
  output [4:0] out_18,
  output [15:0] Immed,
  output [31:0] ALEout,
  output [8:0] out_21,
  output [5:0] out_22,
  output [31:0] out_23
);

  wire CLK, MXBR, not_1_out, not_2_out, not_3_out, or_1_out, RST;
  wire [4:0] multiplexer_2_out;
  wire [31:0] mipsprogramrom_1_p5, multiplexer_1_out, multiplexer_3_out, pc_1_pcout, PC_2_q, SEImmed,
       UPImmed, ZEImmed;

  Clock clock_1 (.out(CLK));
  Button button_1 (.out(RST));
  PC pc_1 (.PCin(PC_2_q), .Immed({Immed[15:6], funct}), .MXBR(MXBR), .PCout(pc_1_pcout));
  Register #(.width(32)) PC_2 (.D(pc_1_pcout), .Q(PC_2_q), .clk(not_1_out), .clr(RST));  // open: en
  not not_1 (not_1_out, CLK);
  ZE u_ZEImmed (.Immed({Immed[15:6], funct}), .SEImmed(ZEImmed));
  UI u_UPImmed (.Immed({Immed[15:6], funct}), .UImmed(UPImmed));
  SE u_SEImmed (.Immed({Immed[15:6], funct}), .SEImmed(SEImmed));
  Multiplexer #(.width(32)) multiplexer_1 (
    .in0(ALEout), .in1(UPImmed), .out(multiplexer_1_out), .sel(out_13), .en(1'b1));
  Multiplexer #(.width(5)) multiplexer_2 (
    .in0(Immed[15:11]), .in1(out_3[20:16]), .out(multiplexer_2_out), .sel(out_11), .en(1'b1));
  // MIPSProgramROM mipsprogramrom_1: pin names not known; wires that end beside it: PC_2_q, CLK, out_14, multiplexer_2_out, mipsprogramrom_1_p5
  Register #(.width(32)) IR (
    .D(mipsprogramrom_1_p5), .Q({opcode, out_3[25:16], Immed[15:6], funct}), .clk(CLK), .clr(RST));  // open: en
  // RegisterFile registerfile_1: pin names not known; wires that end beside it: multiplexer_1_out, out_3[25:21], out_3[20:16], out_1, out_2
  Multiplexer #(.select(2), .width(32)) multiplexer_3 (
    .in0(out_2), .in1(ZEImmed), .in2(SEImmed), .out(multiplexer_3_out), .sel(out_12), .en(1'b1));  // open: in3
  not not_2 (not_2_out, N);
  and and_1 (MXBR, not_2_out, out_17);
  ALE ale_1 (.RA(out_1), .RB(multiplexer_3_out), .Shift(Immed[10:6]), .ALEop(out_16), .N(N), .ALEout(ALEout));
  not not_3 (not_3_out, out_15);
  assign out_23 = out_15 ? out_2 : 32'bz;  // Controlled_Buffer controlled_buffer_1
  RAM #(.addrWidth(24), .dataWidth(32)) ram_1 (
    .addr(ALEout[23:0]), .data(out_23), .sel(1'b1), .clk(CLK), .ld(not_3_out), .clr(RST));
  or or_1 (or_1_out, opcode[0], opcode[1], opcode[2], opcode[4], opcode[5], opcode[3]);
  Multiplexer #(.width(6)) multiplexer_4 (.in0(funct), .in1(opcode), .out(out_22), .sel(or_1_out), .en(1'b1));
  ROM #(.addrWidth(6), .dataWidth(9)) rom_1 (
    .addr(out_22), .data({out_11, out_12, out_13, out_14, out_15, out_16, out_17}));  // open: sel

  assign Immed[5:0] = funct;
  assign {out_3[31:26], out_3[15:0]} = {opcode, Immed[15:6], funct};
  assign out_18 = Immed[10:6];
  assign out_21 = {out_11, out_12, out_13, out_14, out_15, out_16, out_17};
  assign rd = Immed[15:11];
  assign rs = out_3[25:21];
  assign rt = out_3[20:16];
  assign shamt = Immed[10:6];

  // Other names for the same wires on the sheet: A[31:0] = out_1; B[31:0] = out_2; BR = out_17; ALEop[1:0] = out_16;
  //   LD = out_15; WE = out_14; MXWD = out_13; MXB[1:0] = out_12; MXWA = out_11

  // Notes on the sheet:
  //   contents of rom_1 (hex, n*v repeats v):
  //   0 0 14 4*0 7 4*0 152 0 0 130 17*0 18 9*0 188
endmodule

module ALE (
  input  [31:0] RA,
  input  [31:0] RB,
  input  [4:0] Shift,
  input  [1:0] ALEop,
  output N,
  output [31:0] ALEout
);

  wire not_1_out, or_1_out;
  wire [31:0] adder_1_out, and_1_out, shifter_1_out, subtractor_1_out;

  Adder #(.width(32)) adder_1 (.a(RA), .b(RB), .out(adder_1_out));  // open: cin, cout
  assign and_1_out = RA & RB;  // AND_Gate and_1, 32 bits wide
  Shifter #(.width(32), .shift("lr")) shifter_1 (.in(RB), .\dist (Shift), .out(shifter_1_out));
  Subtractor #(.width(32)) subtractor_1 (.a(RA), .b({32{1'b0}}), .out(subtractor_1_out));  // open: bin, bout
  Multiplexer #(.select(2), .width(32)) multiplexer_1 (
    .in0(adder_1_out), .in1(and_1_out), .in2(shifter_1_out), .in3(subtractor_1_out), .out(ALEout),
    .sel(ALEop), .en(1'b1));
  or or_1 (or_1_out, ALEout[15], ALEout[0], ALEout[1], ALEout[2], ALEout[3], ALEout[4], ALEout[5], ALEout[6], ALEout[7], ALEout[8], ALEout[9], ALEout[10], ALEout[11], ALEout[12], ALEout[13], ALEout[14], ALEout[16], ALEout[17], ALEout[18], ALEout[19], ALEout[20], ALEout[21], ALEout[22], ALEout[23], ALEout[24], ALEout[25], ALEout[26], ALEout[27], ALEout[28], ALEout[29], ALEout[30], ALEout[31]);
  nand nand_1 (N, or_1_out, not_1_out);
  not not_1 (not_1_out, ALEout[31]);
endmodule

module BrAddr (
  input  [15:0] Immed,
  output [31:0] BrAddr
);


  assign BrAddr = {{15{Immed[15]}}, Immed[14:0], 2'b00};
endmodule

module ZE (
  input  [15:0] Immed,
  output [31:0] SEImmed
);


  assign SEImmed = {{16{1'b0}}, Immed};
endmodule

module UI (
  input  [15:0] Immed,
  output [31:0] UImmed
);


  assign UImmed = {Immed, {16{1'b0}}};
endmodule

module SE (
  input  [15:0] Immed,
  output [31:0] SEImmed
);


  assign SEImmed = {{17{Immed[15]}}, Immed[14:0]};
endmodule

module PC (
  input  [31:0] PCin,
  input  [15:0] Immed,
  input  MXBR,
  output [31:0] PCout
);

  wire [31:0] adder_1_out, adder_2_out, BrAddr_braddr;

  Adder #(.width(32)) adder_1 (.a(PCin), .b(32'h4), .out(adder_1_out));  // open: cin, cout
  BrAddr BrAddr (.Immed(Immed), .BrAddr(BrAddr_braddr));
  Adder #(.width(32)) adder_2 (.a(adder_1_out), .b(BrAddr_braddr), .out(adder_2_out));  // open: cin, cout
  Multiplexer #(.width(32)) multiplexer_1 (.in0(adder_1_out), .in1(adder_2_out), .out(PCout), .sel(MXBR), .en(1'b1));
endmodule
